// Logisim project wk6ex1-4.circ as structural Verilog: 8 circuits, main circuit MyXOR
module MyXOR (
  input  in_1,
  input  in_2,
  output out_3
);

  wire and_1_out, and_2_out, not_1_out, not_2_out;

  not not_1 (not_1_out, in_2);
  not not_2 (not_2_out, in_1);
  and and_1 (and_1_out, in_1, not_1_out);
  and and_2 (and_2_out, in_2, not_2_out);
  or or_1 (out_3, and_1_out, and_2_out);

  // Notes on the sheet:
  //   Hier kan je een XOR-schakeling bouwen
  //   Je kan de tutorial volgen (in het Help-menu; "tutorial") of zelf de oplossing bedenken...
  //   Gemaakt door; Bas, Freek, Mike & Reinder
endmodule

module FullAdder (
  input  X,
  input  Y,
  input  CarryIn,
  output Sum,
  output CarryOut
);

  wire and_1_out, and_2_out, and_3_out, and_4_out, and_5_out, and_6_out, and_7_out, and_8_out, not_1_out,
       not_2_out, not_3_out;

  not not_1 (not_1_out, X);
  not not_2 (not_2_out, Y);
  not not_3 (not_3_out, CarryIn);
  and and_1 (and_1_out, X, Y, CarryIn);
  and and_2 (and_2_out, X, X, not_3_out, not_2_out);
  and and_3 (and_3_out, not_1_out, Y, not_3_out);
  and and_4 (and_4_out, CarryIn, not_2_out, not_1_out);
  and and_5 (and_5_out, X, Y, CarryIn);
  and and_6 (and_6_out, X, Y, not_3_out);
  and and_7 (and_7_out, X, not_2_out, CarryIn);
  and and_8 (and_8_out, not_1_out, Y, CarryIn);
  or or_1 (Sum, and_1_out, and_2_out, and_3_out, and_4_out);
  or or_2 (CarryOut, and_5_out, and_6_out, and_7_out, and_8_out);

  // Notes on the sheet:
  //   3 invoerbits:  X,  Y en CarryIn
  //   Gemaakt door; Bas, Freek, Mike & Reinder
  //   Hier kan je een FULL-ADDERschakeling bouwen
  //   (1) teken de andere vier rails   (2) je hebt 8 AND-poorten nodig    (3)  je hebt twee OR-poorten nodig
  //   twee uitvoerbits:  Sum en CarryOut
endmodule

module Een_4bit_Ripple_Carry_Adder (
  input  Y3,
  input  X3,
  input  Y2,
  input  X2,
  input  Y1,
  input  X1,
  input  Y0,
  input  X0,
  output Sum4,
  output Sum3,
  output Sum2,
  output Sum1,
  output Sum0
);

  wire fulladder_2_carryout, fulladder_3_carryout, fulladder_4_carryout;

  FullAdder fulladder_1 (.X(X3), .Y(Y3), .CarryIn(fulladder_2_carryout), .Sum(Sum3), .CarryOut(Sum4));
  FullAdder fulladder_2 (.X(X2), .Y(Y2), .CarryIn(fulladder_3_carryout), .Sum(Sum2), .CarryOut(fulladder_2_carryout));
  FullAdder fulladder_3 (.X(X1), .Y(Y1), .CarryIn(fulladder_4_carryout), .Sum(Sum1), .CarryOut(fulladder_3_carryout));
  FullAdder fulladder_4 (.X(X0), .Y(Y0), .CarryIn(1'b0), .Sum(Sum0), .CarryOut(fulladder_4_carryout));

  // Notes on the sheet:
  //   Hier kan je een 4-bit-RIPPLE-CARRY-ADDERschakeling bouwen
  //   Gemaakt door; Bas, Freek, Mike & Reinder
  //   8 invoerbits
  //   5 uitvoerbits
endmodule

module Een_4bit_vermenigvuldiger (
  input  Y3,
  input  Y2,
  input  Y1,
  input  Y0,
  input  X3,
  input  X2,
  input  X1,
  input  X0,
  output Z7,
  output Z6,
  output Z5,
  output Z4,
  output Z3,
  output Z2,
  output Z1,
  output Z0
);

  wire een_4bit_ripple_carry_adder_1_sum1, een_4bit_ripple_carry_adder_1_sum2,
       een_4bit_ripple_carry_adder_1_sum3, een_4bit_ripple_carry_adder_1_sum4,
       een_4bit_ripple_carry_adder_2_sum1, een_4bit_ripple_carry_adder_2_sum2,
       een_4bit_ripple_carry_adder_2_sum3, een_4bit_ripple_carry_adder_2_sum4, een_4x1_vermenigvuldiger_1_z1,
       een_4x1_vermenigvuldiger_1_z2, een_4x1_vermenigvuldiger_1_z3, een_4x1_vermenigvuldiger_2_z0,
       een_4x1_vermenigvuldiger_2_z1, een_4x1_vermenigvuldiger_2_z2, een_4x1_vermenigvuldiger_2_z3,
       een_4x1_vermenigvuldiger_3_z0, een_4x1_vermenigvuldiger_3_z1, een_4x1_vermenigvuldiger_3_z2,
       een_4x1_vermenigvuldiger_3_z3, een_4x1_vermenigvuldiger_4_z0, een_4x1_vermenigvuldiger_4_z1,
       een_4x1_vermenigvuldiger_4_z2, een_4x1_vermenigvuldiger_4_z3;

  Een_4x1_vermenigvuldiger een_4x1_vermenigvuldiger_1 (
    .x(X0), .y3(Y3), .y2(Y2), .y1(Y1), .y0(Y0), .z3(een_4x1_vermenigvuldiger_1_z3),
    .z2(een_4x1_vermenigvuldiger_1_z2), .z1(een_4x1_vermenigvuldiger_1_z1), .z0(Z0));
  Een_4x1_vermenigvuldiger een_4x1_vermenigvuldiger_2 (
    .x(X1), .y3(Y3), .y2(Y2), .y1(Y1), .y0(Y0), .z3(een_4x1_vermenigvuldiger_2_z3),
    .z2(een_4x1_vermenigvuldiger_2_z2), .z1(een_4x1_vermenigvuldiger_2_z1), .z0(een_4x1_vermenigvuldiger_2_z0));
  Een_4x1_vermenigvuldiger een_4x1_vermenigvuldiger_3 (
    .x(X2), .y3(Y3), .y2(Y2), .y1(Y1), .y0(Y0), .z3(een_4x1_vermenigvuldiger_3_z3),
    .z2(een_4x1_vermenigvuldiger_3_z2), .z1(een_4x1_vermenigvuldiger_3_z1), .z0(een_4x1_vermenigvuldiger_3_z0));
  Een_4x1_vermenigvuldiger een_4x1_vermenigvuldiger_4 (
    .x(X3), .y3(Y3), .y2(Y2), .y1(Y1), .y0(Y0), .z3(een_4x1_vermenigvuldiger_4_z3),
    .z2(een_4x1_vermenigvuldiger_4_z2), .z1(een_4x1_vermenigvuldiger_4_z1), .z0(een_4x1_vermenigvuldiger_4_z0));
  Een_4bit_Ripple_Carry_Adder een_4bit_ripple_carry_adder_1 (
    .Y3(een_4x1_vermenigvuldiger_2_z3), .Y2(een_4x1_vermenigvuldiger_2_z2),
    .X2(een_4x1_vermenigvuldiger_1_z3), .Y1(een_4x1_vermenigvuldiger_2_z1),
    .X1(een_4x1_vermenigvuldiger_1_z2), .Y0(een_4x1_vermenigvuldiger_2_z0),
    .X0(een_4x1_vermenigvuldiger_1_z1), .Sum4(een_4bit_ripple_carry_adder_1_sum4),
    .Sum3(een_4bit_ripple_carry_adder_1_sum3), .Sum2(een_4bit_ripple_carry_adder_1_sum2),
    .Sum1(een_4bit_ripple_carry_adder_1_sum1), .Sum0(Z1));  // open: X3
  Een_4bit_Ripple_Carry_Adder een_4bit_ripple_carry_adder_2 (
    .Y3(een_4bit_ripple_carry_adder_1_sum4), .X3(een_4x1_vermenigvuldiger_3_z3),
    .Y2(een_4bit_ripple_carry_adder_1_sum3), .X2(een_4x1_vermenigvuldiger_3_z2),
    .Y1(een_4bit_ripple_carry_adder_1_sum2), .X1(een_4x1_vermenigvuldiger_3_z1),
    .Y0(een_4bit_ripple_carry_adder_1_sum1), .X0(een_4x1_vermenigvuldiger_3_z0),
    .Sum4(een_4bit_ripple_carry_adder_2_sum4), .Sum3(een_4bit_ripple_carry_adder_2_sum3),
    .Sum2(een_4bit_ripple_carry_adder_2_sum2), .Sum1(een_4bit_ripple_carry_adder_2_sum1), .Sum0(Z2));
  Een_4bit_Ripple_Carry_Adder een_4bit_ripple_carry_adder_3 (
    .Y3(een_4bit_ripple_carry_adder_2_sum4), .X3(een_4x1_vermenigvuldiger_4_z3),
    .Y2(een_4bit_ripple_carry_adder_2_sum3), .X2(een_4x1_vermenigvuldiger_4_z2),
    .Y1(een_4bit_ripple_carry_adder_2_sum2), .X1(een_4x1_vermenigvuldiger_4_z1),
    .Y0(een_4bit_ripple_carry_adder_2_sum1), .X0(een_4x1_vermenigvuldiger_4_z0), .Sum4(Z7), .Sum3(Z6),
    .Sum2(Z5), .Sum1(Z4), .Sum0(Z3));

  // Notes on the sheet:
  //   factor (4 bits)
  //   See the problem for details on this hint:   Build a 4x1-bit multiplier first!
  //   tweede factor (4 bits)
  //   Gemaakt door; Bas, Freek, Mike & Reinder
  //   product (8 bits)
  //   4-bit-VERMENIGVULDIGINGSschakeling
  //   meest significante (hoogste) uitvoerbit
  //   minst significante (laagste) uitvoerbit
endmodule

module Een_3bij2_deler (
  input  Y2,
  input  Y1,
  input  Y0,
  input  X1,
  input  X0,
  output Z2,
  output Z1,
  output Z0,
  output Error
);

  wire and_1_out, and_2_out, and_3_out, and_5_out, and_6_out, and_7_out, and_8_out, and_9_out, and_10_out,
       nand_1_out, not_1_out, not_2_out, or_4_out, xor_1_out;

  not not_1 (not_1_out, X1);
  not not_2 (not_2_out, X0);
  and and_1 (and_1_out, X0, Y2, not_1_out);
  and and_2 (and_2_out, X0, Y1, not_1_out);
  and and_3 (and_3_out, X0, Y0, not_1_out);
  // AND_Gate and_4 has open pins: in0=not_2_out, in1=X1, out=open
  and and_5 (and_5_out, not_2_out, X1, Y2);
  and and_6 (and_6_out, not_2_out, X1, Y1);
  and and_7 (and_7_out, X0, X1, Y2);
  and and_8 (and_8_out, X0, X1, Y1, Y1, Y2);
  and and_9 (and_9_out, X0, X1, Y0, Y1);
  xor xor_1 (xor_1_out, and_7_out, and_8_out);
  nand nand_1 (nand_1_out, and_8_out, and_9_out);
  buf or_1 (Z2, and_1_out);  // OR_Gate
  or or_2 (Z1, and_2_out, and_5_out, and_8_out);
  or or_3 (Z0, and_3_out, and_6_out, xor_1_out, and_10_out);
  and and_10 (and_10_out, nand_1_out, and_9_out);
  or or_4 (or_4_out, Z2, Z1, Z0);
  not not_3 (Error, or_4_out);

  // Notes on the sheet:
  //   Teller (3 bits: Y2 Y1 Y0)
  //   Gemaakt door; Bas, Freek, Mike & Reinder
  //   Noemer (2 bits: X1 X0)
  //   3-bij-2-bit-DELINGSschakeling
  //   Quotiënt (4 bits: Z2 Z1 Z0 en Error)
endmodule

module Een_2bit_decoder (
);


  // Notes on the sheet:
  //   2-bit-DECODERschakeling (bonusopgave)
endmodule

module Een_12nGb_geheugen (
);


  // Notes on the sheet:
  //   12-nanogigabit-GEHEUGENschakelin (bonusopgave)
endmodule

module Een_4x1_vermenigvuldiger (
  input  x,
  input  y3,
  input  y2,
  input  y1,
  input  y0,
  output z3,
  output z2,
  output z1,
  output z0
);

  and and_1 (z3, y3, x);
  and and_2 (z2, y2, x);
  and and_3 (z1, y1, x);
  and and_4 (z0, y0, x);

  // Notes on the sheet:
  //   Gemaakt door; Bas, Freek, Mike & Reinder
endmodule
